// Logisim project Gate.circ as structural Verilog: 17 circuits, main circuit main
module main (
  input  in_1,
  input  X,
  input  Y,
  output Sum,
  output Carry
);

  wire and_1_out, and_2_out, and_3_out, and_4_out, and_5_out, and_6_out, and_7_out, not_1_out, not_2_out,
       not_3_out, not_4_out, not_5_out, not_6_out;

  not not_1 (not_1_out, in_1);
  not not_2 (not_2_out, X);
  not not_3 (not_3_out, in_1);
  not not_4 (not_4_out, Y);
  not not_5 (not_5_out, X);
  not not_6 (not_6_out, Y);
  and and_1 (and_1_out, X, Y);
  and and_2 (and_2_out, in_1, Y);
  and and_3 (and_3_out, in_1, X);
  and and_4 (and_4_out, not_1_out, not_2_out, Y);
  and and_5 (and_5_out, not_3_out, X, not_4_out);
  and and_6 (and_6_out, in_1, not_5_out, not_6_out);
  and and_7 (and_7_out, in_1, X, Y);
  or or_1 (Carry, and_1_out, and_2_out, and_3_out);
  or or_2 (Sum, and_4_out, and_5_out, and_6_out, and_7_out);
endmodule

module Full_Adder (
  input  Cin,
  input  X,
  input  Y,
  output Sum,
  output Carry
);

  wire and_1_out, and_2_out, and_3_out, and_4_out, and_5_out, and_6_out, and_7_out, not_1_out, not_2_out,
       not_3_out, not_4_out, not_5_out, not_6_out;

  not not_1 (not_1_out, Cin);
  not not_2 (not_2_out, X);
  not not_3 (not_3_out, Cin);
  not not_4 (not_4_out, Y);
  not not_5 (not_5_out, X);
  not not_6 (not_6_out, Y);
  and and_1 (and_1_out, X, Y);
  and and_2 (and_2_out, Cin, Y);
  and and_3 (and_3_out, Cin, X);
  and and_4 (and_4_out, not_1_out, not_2_out, Y);
  and and_5 (and_5_out, not_3_out, X, not_4_out);
  and and_6 (and_6_out, Cin, not_5_out, not_6_out);
  and and_7 (and_7_out, Cin, X, Y);
  or or_1 (Carry, and_1_out, and_2_out, and_3_out);
  or or_2 (Sum, and_4_out, and_5_out, and_6_out, and_7_out);
endmodule

module Parallel_Adder (
  input  Cin,
  input  [3:0] A3_A2_A1_A0,
  input  [3:0] B3_B2_B1_B0,
  output [3:0] SUM,
  output Carry_Out
);

  wire full_adder_1_p5, full_adder_2_p5, full_adder_3_p5;

  // Lab_Session_01_Full_Adder full_adder_1: pin names not known; wires that end beside it: Cin, A3_A2_A1_A0[0], B3_B2_B1_B0[0], SUM[0], full_adder_1_p5
  // Lab_Session_01_Full_Adder full_adder_2: pin names not known; wires that end beside it: full_adder_1_p5, A3_A2_A1_A0[1], B3_B2_B1_B0[1], SUM[1], full_adder_2_p5
  // Lab_Session_01_Full_Adder full_adder_3: pin names not known; wires that end beside it: full_adder_2_p5, A3_A2_A1_A0[2], B3_B2_B1_B0[2], SUM[2], full_adder_3_p5
  // Lab_Session_01_Full_Adder full_adder_4: pin names not known; wires that end beside it: full_adder_3_p5, A3_A2_A1_A0[3], B3_B2_B1_B0[3], SUM[3], Carry_Out

  // Notes on the sheet:
  //   LSB
  //   MSB
endmodule

module Adder_Subtractor (
  input  Cin,
  input  [3:0] A3_A2_A1_A0,
  input  [3:0] in_3,
  output [3:0] Y3_Y2_Y1_Y0,
  output Carry_Out
);

  wire full_adder_1_carry, full_adder_2_carry, full_adder_3_carry, xor_1_out, xor_2_out, xor_3_out;

  xor xor_1 (xor_1_out, Cin, in_3[0]);
  xor xor_2 (xor_2_out, Cin, in_3[1]);
  xor xor_3 (xor_3_out, Cin, in_3[2]);
  xor xor_4 (A3_A2_A1_A0[3], Cin, in_3[3]);
  Full_Adder full_adder_1 (
    .Cin(Cin), .X(A3_A2_A1_A0[0]), .Y(xor_1_out), .Sum(Y3_Y2_Y1_Y0[0]), .Carry(full_adder_1_carry));
  Full_Adder full_adder_2 (
    .Cin(full_adder_1_carry), .X(A3_A2_A1_A0[1]), .Y(xor_2_out), .Sum(Y3_Y2_Y1_Y0[1]),
    .Carry(full_adder_2_carry));
  Full_Adder full_adder_3 (
    .Cin(full_adder_2_carry), .X(A3_A2_A1_A0[2]), .Y(xor_3_out), .Sum(Y3_Y2_Y1_Y0[2]),
    .Carry(full_adder_3_carry));
  Full_Adder full_adder_4 (
    .Cin(full_adder_3_carry), .X(A3_A2_A1_A0[3]), .Y(A3_A2_A1_A0[3]), .Sum(Y3_Y2_Y1_Y0[3]), .Carry(Carry_Out));

  // Notes on the sheet:
  //   XOR
  //   XOR
  //   XOR
  //   XOR
  //   FA1
  //   FA2
  //   FA3
  //   FA4
endmodule

module _4x1_Mux (
  input  D0,
  input  D1,
  input  D2,
  input  D3,
  input  S1,
  input  S0,
  output Y
);

  wire and_1_out, and_2_out, and_3_out, and_4_out, not_1_out, not_2_out, not_3_out, not_4_out;

  not not_1 (not_1_out, S1);
  not not_2 (not_2_out, S0);
  not not_3 (not_3_out, S1);
  not not_4 (not_4_out, S0);
  and and_1 (and_1_out, not_1_out, not_2_out, D0);
  and and_2 (and_2_out, not_3_out, S0, D1);
  and and_3 (and_3_out, S1, not_4_out, D2);
  and and_4 (and_4_out, S1, S0, D3);
  or or_1 (Y, and_1_out, and_2_out, and_3_out, and_4_out);
endmodule

module SingleBitAU (
  input  Cin,
  input  A0,
  input  B0,
  input  Constant1,
  input  S0,
  input  S1,
  output D0,
  output Carry_out
);

  wire not_1_out, not_2_out;

  not not_1 (not_1_out, B0);
  not not_2 (not_2_out, Constant1);
  // _4_to_1_MUX 4_to_1_mux_1: pin names not known; wires that end beside it: B0, not_1_out, Constant1, not_2_out, S0, S1, A0
  // COALAB_Full_Adder full_adder_1: pin names not known; wires that end beside it: Cin, D0, Carry_out
endmodule

module SingleLogic (
  input  A0,
  input  B0,
  input  S2,
  input  S1,
  output Y0
);

  wire and_1_out, not_1_out, or_1_out, xor_1_out;

  not not_1 (not_1_out, A0);
  and and_1 (and_1_out, A0, B0);
  or or_1 (or_1_out, A0, B0);
  xor xor_1 (xor_1_out, A0, B0);
  // _4_to_1_MUX 4_to_1_mux_1: pin names not known; wires that end beside it: and_1_out, or_1_out, xor_1_out, not_1_out, S1, S2, Y0
endmodule

module _4_Bit_AU (
  input  Cin,
  input  [3:0] B0_B1_B2_B3,
  input  [3:0] A0_A1_A2_A3,
  input  [3:0] Constant,
  input  S1,
  input  S0,
  output [3:0] D3_D2_D1_D0,
  output Overflow,
  output Carry_Out
);

  wire singlebitau_1_carry_out, singlebitau_2_carry_out, singlebitau_3_carry_out;

  SingleBitAU singlebitau_1 (
    .Cin(Cin), .A0(B0_B1_B2_B3[0]), .B0(A0_A1_A2_A3[0]), .Constant1(Constant[0]), .S0(S1), .S1(S0),
    .D0(D3_D2_D1_D0[0]), .Carry_out(singlebitau_1_carry_out));
  SingleBitAU singlebitau_2 (
    .Cin(singlebitau_1_carry_out), .A0(B0_B1_B2_B3[1]), .B0(A0_A1_A2_A3[1]), .Constant1(Constant[1]),
    .S0(S1), .S1(S0), .D0(D3_D2_D1_D0[1]), .Carry_out(singlebitau_2_carry_out));
  SingleBitAU singlebitau_3 (
    .Cin(singlebitau_2_carry_out), .A0(B0_B1_B2_B3[2]), .B0(A0_A1_A2_A3[2]), .Constant1(Constant[2]),
    .S0(S1), .S1(S0), .D0(D3_D2_D1_D0[2]), .Carry_out(singlebitau_3_carry_out));
  SingleBitAU singlebitau_4 (
    .Cin(singlebitau_3_carry_out), .A0(B0_B1_B2_B3[3]), .B0(A0_A1_A2_A3[3]), .Constant1(Constant[3]),
    .S0(S1), .S1(S0), .D0(D3_D2_D1_D0[3]), .Carry_out(Carry_Out));
  xor xor_1 (Overflow, singlebitau_3_carry_out, Carry_Out);
endmodule

module _4_Stage_Logic_Unit (
  input  [3:0] B3_B2_B1_B0,
  input  S1,
  input  S0,
  input  [3:0] A3_A2_A1_A0,
  output [3:0] Y3_Y2_Y1_Y0
);

  SingleLogic singlelogic_1 (.A0(B3_B2_B1_B0[0]), .B0(A3_A2_A1_A0[0]), .S1(S0), .S2(S1), .Y0(Y3_Y2_Y1_Y0[0]));
  SingleLogic singlelogic_2 (.A0(B3_B2_B1_B0[1]), .B0(A3_A2_A1_A0[1]), .S1(S0), .S2(S1), .Y0(Y3_Y2_Y1_Y0[1]));
  SingleLogic singlelogic_3 (.A0(B3_B2_B1_B0[2]), .B0(A3_A2_A1_A0[2]), .S1(S0), .S2(S1), .Y0(Y3_Y2_Y1_Y0[2]));
  SingleLogic singlelogic_4 (.A0(B3_B2_B1_B0[3]), .B0(A3_A2_A1_A0[3]), .S1(S0), .S2(S1), .Y0(Y3_Y2_Y1_Y0[3]));
endmodule

module _2x1_Single_Bit_Mux (
  input  D0,
  input  D1,
  input  S,
  output Y
);

  wire and_1_out, and_2_out, not_1_out;

  not not_1 (not_1_out, S);
  and and_1 (and_1_out, not_1_out, D0);
  and and_2 (and_2_out, S, D1);
  or or_1 (Y, and_1_out, and_2_out);
endmodule

module _2x1_Multi_bit_Mux (
  input  [3:0] A,
  input  [3:0] B,
  input  Select,
  output [3:0] out_4
);

  // _2_to_1_Single_Bit_MUX 2_to_1_single_bit_mux_1: pin names not known; wires that end beside it: A[0], B[0], Select, out_4[0]
  // _2_to_1_Single_Bit_MUX 2_to_1_single_bit_mux_2: pin names not known; wires that end beside it: A[1], B[1], Select, out_4[1]
  // _2_to_1_Single_Bit_MUX 2_to_1_single_bit_mux_3: pin names not known; wires that end beside it: A[2], B[2], Select, out_4[2]
  // _2_to_1_Single_Bit_MUX 2_to_1_single_bit_mux_4: pin names not known; wires that end beside it: A[3], B[3], Select, out_4[3]
endmodule

module _4_Bit_ALU (
  input  Cin,
  input  [3:0] B,
  input  [3:0] A,
  input  S2,
  input  S1,
  input  S0,
  input  [3:0] Constant,
  output Carry___SIgn,
  output Overflow,
  output [3:0] Y
);

  wire n4_bit_arithmetic_unit_1_p7, n4_stage_logic_unit_1_p5;

  // _4_Bit_Arithmetic_Unit 4_bit_arithmetic_unit_1: pin names not known; wires that end beside it: Cin, B, A, Constant, S1, S0, n4_bit_arithmetic_unit_1_p7, Overflow, Carry___SIgn
  // lab4_4_Stage_Logic_Unit 4_stage_logic_unit_1: pin names not known; wires that end beside it: B, S1, S0, A, n4_stage_logic_unit_1_p5
  // _2_to_1_Multi_Bit_MUX 2_to_1_multi_bit_mux_1: pin names not known; wires that end beside it: n4_bit_arithmetic_unit_1_p7, n4_stage_logic_unit_1_p5, S2, Y

  // Notes on the sheet:
  //   4 Bit AU
  //   4 Bit LU
  //   2 to 1 Multibit MUX
endmodule

module Decoder (
  input  S0,
  input  S1,
  output D0,
  output D1,
  output D2,
  output D3
);

  wire nand_1_out, nand_2_out, nand_3_out, nand_4_out, nand_5_out, nand_6_out, nand_7_out, nand_8_out,
       nand_9_out, nand_10_out, nand_11_out, nand_12_out, nand_13_out, nand_14_out, nand_15_out, nand_16_out;

  nand nand_1 (nand_1_out, S0, S0);
  nand nand_2 (nand_2_out, S1, S1);
  nand nand_3 (nand_3_out, S0, S0);
  nand nand_4 (nand_4_out, S1, S1);
  nand nand_5 (nand_5_out, S0, S0);
  nand nand_6 (nand_6_out, S0, S0);
  nand nand_7 (nand_7_out, S1, S1);
  nand nand_8 (nand_8_out, S1, S1);
  nand nand_9 (nand_9_out, S0, S1);
  nand nand_10 (nand_10_out, S0, S1);
  nand nand_11 (nand_11_out, nand_1_out, nand_2_out);
  nand nand_12 (nand_12_out, nand_3_out, nand_4_out);
  nand nand_13 (nand_13_out, nand_5_out, S1);
  nand nand_14 (nand_14_out, nand_6_out, S1);
  nand nand_15 (nand_15_out, S0, nand_7_out);
  nand nand_16 (nand_16_out, S0, nand_8_out);
  nand nand_17 (D3, nand_9_out, nand_10_out);
  nand nand_18 (D0, nand_11_out, nand_12_out);
  nand nand_19 (D1, nand_13_out, nand_14_out);
  nand nand_20 (D2, nand_15_out, nand_16_out);
endmodule

module MultiBit_Mux (
  input  S0,
  input  S1,
  input  [3:0] A,
  input  [3:0] in_4,
  input  [3:0] C,
  input  [3:0] D,
  output [3:0] out_7
);

  // _4_to_1_MUX 4_to_1_mux_1: pin names not known; wires that end beside it: A[0], in_4[0], C[0], D[0], S1, S0, out_7[0]
  // _4_to_1_MUX 4_to_1_mux_2: pin names not known; wires that end beside it: A[1], in_4[1], C[1], D[1], S1, S0, out_7[1]
  // _4_to_1_MUX 4_to_1_mux_3: pin names not known; wires that end beside it: A[2], in_4[2], C[2], D[2], S1, S0, out_7[2]
  // _4_to_1_MUX 4_to_1_mux_4: pin names not known; wires that end beside it: A[3], in_4[3], C[3], D[3], S1, S0, out_7[3]

  // Notes on the sheet:
  //   B
endmodule

module Register_File (
  input  [1:0] in_1,
  input  WireEnable,
  input  [1:0] in_3,
  input  [1:0] RegRead2,
  input  [3:0] in_5,
  output [3:0] ReadPort1,
  output [3:0] ReadPort2
);

  wire and_1_out, and_2_out, and_3_out, and_4_out, clock_1_out, decoder_1_p3, decoder_1_p4, decoder_1_p5,
       decoder_1_p6;
  wire [3:0] register_1_q, register_2_q, register_3_q, register_4_q;

  // Lab_Session_05_Real_Decoder decoder_1: pin names not known; wires that end beside it: in_3[0], in_3[1], decoder_1_p3, decoder_1_p4, decoder_1_p5, decoder_1_p6
  and and_1 (and_1_out, WireEnable, decoder_1_p3);
  and and_2 (and_2_out, WireEnable, decoder_1_p4);
  and and_3 (and_3_out, WireEnable, decoder_1_p5);
  and and_4 (and_4_out, WireEnable, decoder_1_p6);
  Clock clock_1 (.out(clock_1_out));
  Register #(.width(4)) register_1 (.D(in_5), .en(and_1_out), .Q(register_1_q), .clr(clock_1_out));  // open: clk
  Register #(.width(4)) register_2 (.D(in_5), .en(and_2_out), .Q(register_2_q), .clr(clock_1_out));  // open: clk
  Register #(.width(4)) register_3 (.D(in_5), .en(and_3_out), .Q(register_3_q), .clr(clock_1_out));  // open: clk
  Register #(.width(4)) register_4 (.D(in_5), .en(and_4_out), .Q(register_4_q), .clr(clock_1_out));  // open: clk
  // Multibit_MUX multibit_mux_1: pin names not known; wires that end beside it: register_1_q, register_2_q, register_3_q, register_4_q, in_1[1], in_1[0], ReadPort1
  // Multibit_MUX multibit_mux_2: pin names not known; wires that end beside it: register_1_q, register_2_q, register_3_q, register_4_q, RegRead2[0], RegRead2[1], ReadPort2

  // Notes on the sheet:
  //   DataInput
  //   Decoder
  //   Clock
  //   Register
  //   RegRead1
endmodule

module ALU_and_Register_File (
  input  [1:0] in_1,
  input  WireEnable,
  input  [2:0] in_3,
  input  in_4,
  input  [1:0] in_5,
  input  [1:0] RegRead2,
  input  [3:0] in_7,
  input  [3:0] in_8,
  output OverFlow,
  output out_10,
  output [3:0] out_11
);

  wire and_1_out, and_2_out, and_3_out, and_4_out, clock_1_out, decoder_1_p3, decoder_1_p4, decoder_1_p5,
       decoder_1_p6;
  wire [3:0] multibit_mux_1_p7, multibit_mux_2_p7, register_1_q, register_2_q, register_3_q, register_4_q;

  // Lab_Session_05_Real_Decoder decoder_1: pin names not known; wires that end beside it: in_5[0], in_5[1], decoder_1_p3, decoder_1_p4, decoder_1_p5, decoder_1_p6
  and and_1 (and_1_out, WireEnable, decoder_1_p3);
  and and_2 (and_2_out, WireEnable, decoder_1_p4);
  and and_3 (and_3_out, WireEnable, decoder_1_p5);
  and and_4 (and_4_out, WireEnable, decoder_1_p6);
  Clock clock_1 (.out(clock_1_out));
  Register #(.width(4)) register_1 (.D(in_8), .en(and_1_out), .Q(register_1_q), .clr(clock_1_out));  // open: clk
  Register #(.width(4)) register_2 (.D(in_8), .en(and_2_out), .Q(register_2_q), .clr(clock_1_out));  // open: clk
  Register #(.width(4)) register_3 (.D(in_8), .en(and_3_out), .Q(register_3_q), .clr(clock_1_out));  // open: clk
  Register #(.width(4)) register_4 (.D(in_8), .en(and_4_out), .Q(register_4_q), .clr(clock_1_out));  // open: clk
  // Multibit_MUX multibit_mux_1: pin names not known; wires that end beside it: register_1_q, register_2_q, register_3_q, register_4_q, in_1[1], in_1[0], multibit_mux_1_p7
  // Multibit_MUX multibit_mux_2: pin names not known; wires that end beside it: register_1_q, register_2_q, register_3_q, register_4_q, RegRead2[0], RegRead2[1], multibit_mux_2_p7
  _4_Bit_ALU u_4_bit_alu_1 (
    .Cin(in_4), .B(multibit_mux_2_p7), .A(multibit_mux_1_p7), .Constant(in_7), .S2(in_3[2]), .S1(in_3[1]),
    .S0(in_3[0]), .Carry___SIgn(OverFlow), .Overflow(out_10), .Y(out_11));

  // Notes on the sheet:
  //   DataInput
  //   Decoder
  //   Clock
  //   Register
  //   RegRead1
  //   Constant
  //   ALU
  //   Carry/Sign
  //   Y3YY1Y0
endmodule

module _4_Bit_Sequential_Multiplier (
  input  [3:0] Output,
  input  EN,
  input  CLR,
  input  En_2,
  input  CLR_2,
  input  in_6,
  input  Data,
  input  [3:0] in_8,
  input  in_9,
  input  [3:0] Y,
  input  [3:0] Bunch_of_Zeros,
  input  [3:0] Multiplicand,
  output out_13
);

  wire _2_to_1_Multi_Bit_MUX_p4, _2_to_1_Single_Bit_MUX_p2, Clock_out, d_ff_5_q, d_ff_6_q, d_ff_7_q,
       n2_to_1_single_bit_mux_1_p2, n2_to_1_single_bit_mux_2_p2, n2_to_1_single_bit_mux_3_p2;

  Clock Clock (.out(Clock_out));
  // _2_to_1_Single_Bit_MUX _2_to_1_Single_Bit_MUX: pin names not known; wires that end beside it: Data, _2_to_1_Single_Bit_MUX_p2, in_8[3], in_6
  D_Flip_Flop d_ff_1 (
    .clk(Clock_out), .D(_2_to_1_Single_Bit_MUX_p2), .Q(Output[0]), .en(EN), .reset(CLR));  // open: Qn, preset
  // _2_to_1_Single_Bit_MUX 2_to_1_single_bit_mux_1: pin names not known; wires that end beside it: Output[0], n2_to_1_single_bit_mux_1_p2, in_8[2], in_6
  D_Flip_Flop d_ff_2 (
    .clk(Clock_out), .D(n2_to_1_single_bit_mux_1_p2), .Q(Output[1]), .en(EN), .reset(CLR));  // open: Qn, preset
  // _2_to_1_Single_Bit_MUX 2_to_1_single_bit_mux_2: pin names not known; wires that end beside it: Output[1], n2_to_1_single_bit_mux_2_p2, in_8[1], in_6
  D_Flip_Flop d_ff_3 (
    .clk(Clock_out), .D(n2_to_1_single_bit_mux_2_p2), .Q(Output[2]), .en(EN), .reset(CLR));  // open: Qn, preset
  // _2_to_1_Single_Bit_MUX 2_to_1_single_bit_mux_3: pin names not known; wires that end beside it: Output[2], n2_to_1_single_bit_mux_3_p2, in_8[0], in_6
  Parallel_Adder Parallel_Adder (.Cin(in_9), .A3_A2_A1_A0(Y), .B3_B2_B1_B0(Output), .SUM(in_8), .Carry_Out(out_13));
  D_Flip_Flop d_ff_4 (
    .clk(Clock_out), .D(n2_to_1_single_bit_mux_3_p2), .Q(Output[3]), .en(EN), .reset(CLR));  // open: Qn, preset
  // _2_to_1_Multi_Bit_MUX _2_to_1_Multi_Bit_MUX: pin names not known; wires that end beside it: Bunch_of_Zeros, Y, Multiplicand, _2_to_1_Multi_Bit_MUX_p4
  D_Flip_Flop d_ff_5 (.clk(Clock_out), .D(Output[3]), .Q(d_ff_5_q), .en(En_2), .reset(CLR_2));  // open: Qn, preset
  D_Flip_Flop d_ff_6 (.clk(Clock_out), .D(d_ff_5_q), .Q(d_ff_6_q), .en(En_2), .reset(CLR_2));  // open: Qn, preset
  D_Flip_Flop d_ff_7 (.clk(Clock_out), .D(d_ff_6_q), .Q(d_ff_7_q), .en(En_2), .reset(CLR_2));  // open: Qn, preset
  D_Flip_Flop d_ff_8 (
    .clk(Clock_out), .D(d_ff_7_q), .Q(_2_to_1_Multi_Bit_MUX_p4), .en(En_2), .reset(CLR_2));  // open: Qn, preset
endmodule
